// Logisim project cpu.circ as structural Verilog: 1 circuit, main circuit cpu
module cpu (
  input  clk,
  input  [31:0] INSTRUCTION,
  input  [31:0] READ_DATA,
  output [31:0] WRITE_ADDRESS,
  output [31:0] PROGRAM_COUNTER,
  output [31:0] ra,
  output [31:0] sp,
  output [31:0] t0,
  output [31:0] t1,
  output [31:0] t2,
  output [31:0] s0,
  output [31:0] s1,
  output [31:0] a0,
  output [31:0] tohost,
  output [3:0] WRITE_ENABLE,
  output [31:0] WRITE_DATA
);

  wire BSel, RegWEn;
  wire [1:0] WBSel;
  wire [2:0] ImmSel;
  wire [3:0] ALUSel;
  wire [31:0] alu_1_result, imm, PC4, read_reg1, read_reg2, Write_Data_t;

  Adder #(.width(32)) adder_1 (.a(PROGRAM_COUNTER), .b(32'h4), .out(PC4));  // open: cin, cout
  Register #(.width(32)) PC (.D(PC4), .clk(clk), .Q(PROGRAM_COUNTER));  // open: en, clr
  control_logic control_logic_1 (
    .RegWEn(RegWEn), .ImmSel(ImmSel), .BSel(BSel), .ALUSel(ALUSel), .WBSel(WBSel));  // open: CSRWen, PCSel, BrUn, ASel, MemRW, CSRSel, inst, BrEq, BrLt
  imm_gen imm_gen_1 (.inst({INSTRUCTION[31:20], {20{1'b0}}}), .ImmSel(ImmSel), .imm(imm));
  regfile regfile_1 (
    .rs1(INSTRUCTION[19:15]), .rd(INSTRUCTION[11:7]), .Write_Data(Write_Data_t), .RegWEn(RegWEn), .clk(clk),
    .ra(ra), .sp(sp), .t0(t0), .t1(t1), .t2(t2), .s0(s0), .s1(s1), .a0(a0), .Read_Data_1(read_reg1),
    .Read_Data_2(read_reg2));  // open: rs2
  // branch_comp branch_comp_1: pin names not known
  Multiplexer #(.enable("false"), .width(32)) multiplexer_1 (.in0(read_reg2), .in1(imm), .sel(BSel));  // open: out
  alu alu_1 (.Result(alu_1_result), .A(read_reg1), .B(imm), .ALUSel(ALUSel));
  // csr csr_1: pin names not known; wires that end beside it: tohost
  Multiplexer #(.enable("false"), .select(2), .width(32)) multiplexer_2 (
    .in1(alu_1_result), .in2(READ_DATA), .in3(PC4), .out(Write_Data_t), .sel(WBSel));  // open: in0

  // Other names for the same wires on the sheet: rd[4:0] = INSTRUCTION[11:7]; rs1[4:0] = INSTRUCTION[19:15];
  //   immInstr[11:0] = INSTRUCTION[31:20]

  // Notes on the sheet:
  //   Output to IMEM
  //   IMEM (do **NOT** move this)
  //   Inputs from IMEM
  //   It is OK to move the PC, RegFile, ALU, MEM, Branch Comp, Imm Gen, and Control Logic to wherever is most convenient for you when constructing your CPU, and to delete this text
  //   Inputs/Outputs for testing. Do **NOT** move these.
  //   Outputs To DMEM
  //   DMEM (do **NOT** move this)
  //   Inputs From DMEM
endmodule
